# Fritzing sketch L298N_DC_Motor (saved by Fritzing 0.9.3b)
breadboards: 1

parts:
  S1 = H-Bridge with L298N
  부품1 = Arduino Uno (Rev3)
  M1 = DC Motor
  M2 = DC Motor  # not connected
  BAT1 = BC9VPC [package=bc9vpc]

nets:
  N1: S1.12V, BAT1.V+
  GND: S1.GND, 부품1.GND, BAT1.V-
  N2: S1.IN1, 부품1.D4
  N3: S1.IN2, 부품1.D5_PWM
  N4: S1.IN3, 부품1.D6_PWM
  N5: S1.IN4, 부품1.D7
  N6: S1.OUT4-Motor2, M1.pin_1

custom parts:
  H-Bridge with L298N: h-bridge
