# Fritzing sketch L298N_DC_Motor_USound1 (saved by Fritzing 0.9.3b)
breadboards: 1

parts:
  S1 = H-Bridge with L298N
  부품1 = Arduino Uno (Rev3)
  M1 = DC Motor
  M2 = DC Motor  # not connected
  BAT1 = BC9VPC [package=bc9vpc]
  hc-sr1 = hc-sr04

nets:
  N1: S1.12V, BAT1.V+
  GND: S1.GND, 부품1.GND, BAT1.V-, hc-sr1.GND
  N2: S1.IN1, 부품1.D4
  N3: S1.IN2, 부품1.D5_PWM
  N4: S1.IN3, 부품1.D6_PWM
  N5: S1.IN4, 부품1.D7
  N6: S1.OUT4-Motor2, M1.pin_1
  N7: 부품1.A4/SDA, hc-sr1.Trig
  N8: 부품1.A5/SCL, hc-sr1.Echo
  5V: 부품1.5V, hc-sr1.VCC

custom parts:
  H-Bridge with L298N: h-bridge
