# Fritzing sketch L298N_DC_Motor_USound5_BT (saved by Fritzing 0.9.3b)
breadboards: 1

parts:
  S1 = H-Bridge with L298N
  부품1 = Arduino Uno (Rev3)
  M1 = DC Motor
  M2 = DC Motor  # not connected
  BAT1 = BC9VPC [package=bc9vpc]
  hc-sr1 = hc-sr04
  hc-sr2 = hc-sr04
  hc-sr3 = hc-sr04
  hc-sr4 = hc-sr04
  hc-sr5 = hc-sr04
  부품3 = Bluetooth Module Breakout - Roving Networks (RN-41)

nets:
  N1: S1.12V, BAT1.V+
  GND: S1.GND, 부품1.GND, BAT1.V-, hc-sr1.GND, hc-sr2.GND, hc-sr3.GND, hc-sr4.GND, hc-sr5.GND, 부품3.GND
  N2: S1.IN1, 부품1.D4
  N3: S1.IN2, 부품1.D5_PWM
  N4: S1.IN3, 부품1.D6_PWM
  N5: S1.IN4, 부품1.D7
  N6: S1.OUT4-Motor2, M1.pin_1
  N7: 부품1.A0, hc-sr3.Trig
  N8: 부품1.A1, hc-sr3.Echo
  N9: 부품1.A2, hc-sr2.Trig
  N10: 부품1.A3, hc-sr2.Echo
  N11: 부품1.A4/SDA, hc-sr1.Trig
  N12: 부품1.A5/SCL, hc-sr1.Echo
  N13: 부품1.D8, hc-sr4.Echo
  N14: 부품1.D9_PWM, hc-sr4.Trig
  N15: 부품1.D10_PWM/SS, hc-sr5.Echo
  N16: 부품1.D11_PWM/MOSI, hc-sr5.Trig
  N17: 부품1.D12/MISO, 부품3.UARTTX
  N18: 부품1.D13/SCK, 부품3.UARTRX
  3V3: 부품1.3V3, 부품3.VCC
  VCC: 부품1.5V, hc-sr1.VCC, hc-sr2.VCC, hc-sr3.VCC, hc-sr4.VCC, hc-sr5.VCC

custom parts:
  H-Bridge with L298N: h-bridge
