# Fritzing sketch ultrasound (saved by Fritzing 0.9.3b)
breadboards: 1

parts:
  부품1 = Arduino Nano (Rev3.0)
  hc-sr1 = hc-sr04
  hc-sr2 = hc-sr04
  hc-sr3 = hc-sr04
  hc-sr4 = hc-sr04

nets:
  GND: 부품1.GND, hc-sr1.GND, hc-sr2.GND, hc-sr3.GND, hc-sr4.GND
  N1: 부품1.D3, hc-sr1.Trig
  N2: 부품1.D4, hc-sr1.Echo
  N3: 부품1.D7, hc-sr2.Trig
  N4: 부품1.D8, hc-sr2.Echo
  N5: 부품1.D9, hc-sr3.Trig
  N6: 부품1.D10, hc-sr3.Echo
  N7: 부품1.D11/MOSI, hc-sr4.Trig
  N8: 부품1.D12/MISO, hc-sr4.Echo
  VCC: 부품1.5V, hc-sr1.VCC, hc-sr2.VCC, hc-sr3.VCC, hc-sr4.VCC
